# Fritzing sketch RGB LED Wiring (saved by Fritzing 0.9.1b)
breadboards: 1

parts:
  Raspberry_Pi1 = Raspberry Pi B+
  R1 = Resistor [tolerance=±2% resistance=470 package=THT]
  R2 = Resistor [tolerance=±5% resistance=470 package=THT]
  R3 = Resistor [tolerance=±5% resistance=470 package=THT]
  LED1 = RGB LED (com. cathode, rgb) [package="5 mm [THT]"]

nets:
  N1: Raspberry_Pi1.GND, LED1.common_cathode
  N2: Raspberry_Pi1.GPIO17, R1.Pin_0
  N3: Raspberry_Pi1.GPIO27, R2.Pin_0
  N4: Raspberry_Pi1.GPIO18, R3.Pin_0
  N5: R1.Pin_1, LED1.red_anode
  N6: R2.Pin_1, LED1.green_anode
  N7: R3.Pin_1, LED1.blue_anode
